# Fritzing sketch NodeMCU RGB (saved by Fritzing 0.9.3b)
breadboards: 1

parts:
  U1 = NodeMCU V1.0
  RGB_LED = RGB LED - (4 legs) [package="5 mm [THT]"]

nets:
  N1: U1.GND, RGB_LED.common_anode
  N2: U1.D5, RGB_LED.red_cathode
  N3: U1.D6, RGB_LED.green_cathode
  N4: U1.D7, RGB_LED.blue_cathode

custom parts:
  NodeMCU V1.0: ESP8266 based NodeMCU
