# Fritzing sketch NodeMCU_Star_Trek_Sim (saved by Fritzing 0.9.3b)
breadboards: 1

parts:
  U1 = NodeMCU V1.0
  RGB_LED = RGB LED - (4 legs) [package="5 mm [THT]"]
  RED_LED = LED - 5mm [color="Red (633nm)" package="5 mm [THT]"]
  Buzzer = Piezo Speaker
  R1 = Resistor [tolerance=±5% resistance=220 package=THT]

nets:
  N1: U1.D4, RED_LED.anode
  N2: U1.GND, Buzzer.pin1, R1.Pin_1
  N3: U1.D5, RGB_LED.green_cathode
  N4: U1.D6, RGB_LED.blue_cathode
  N5: U1.D7, RGB_LED.red_cathode
  N6: U1.D8, Buzzer.pin2
  N7: RGB_LED.common_anode, RED_LED.cathode, R1.Pin_0

custom parts:
  NodeMCU V1.0: ESP8266 based NodeMCU
