# Fritzing sketch Home Automation Alexa FauxmoESP (saved by Fritzing 0.9.3b)
breadboards: 1

parts:
  U1 = 4-Channel 5v Relay Shield [package=relay-4ch5v10a]
  U2 = NodeMCU V1.0
  External = Power Jack [part_number="POWER 5V" package=power_jack_smd]

nets:
  N1: U1.VCC, External.GNDBREAK
  GND: U1.GND, U2.GND, External.GND
  N2: U1.IN1, U2.D6
  N3: U1.IN2, U2.D7
  N4: U1.IN4, U2.RX
  N5: U1.IN3, U2.D8

notes:
  OUTLET 2
  OUTLET 1
  LIGHT 1
  LIGHT 2

custom parts:
  4-Channel 5v Relay Shield: 4 Channel 5v Relay Shield w. 2x SPD-06VDC-SD-C
  NodeMCU V1.0: ESP8266 based NodeMCU
